// Logisim project Circuito.circ as structural Verilog
// clock
module main (
);

  wire clock, comparator_1_eq, decoder_1_out0, decoder_1_out1, decoder_1_out2, decoder_1_out3,
       decoder_1_out4, decoder_1_out5, decoder_1_out6, decoder_1_out7, decoder_1_out8, decoder_1_out9,
       decoder_1_out10, decoder_1_out11, decoder_1_out12, decoder_1_out14, store_enable, Write;
  wire [4:0] Destino, Destino2_q, Destino_q, NOp1_q, NOp2_q, OpCode2_q, OpCode3_q, OpCode_q,
       translator_1_translatedc;
  wire [13:0] counter_1_q, store_addr_in;
  wire [31:0] adder_1_out, ALU1_result, Imm2_q, Imm_q, InstFetch_q, multiplexer_1_out, ram_1_dout, Regs_op1,
       Regs_op2, store_base_position, store_offset_2_q, store_offset_q, store_write_data, store_write_in,
       WriteData;

  Counter #(.max('h3fff), .width(14)) counter_1 (.clk(clock), .Q(counter_1_q));  // open: clr, load, up, count, D, carry
  RAM #(.addrWidth(14), .dataWidth(32)) ram_1 (
    .addr(counter_1_q), .clk(clock), .dout(ram_1_dout));  // open: we, oe, din
  RAM #(.addrWidth(14), .dataWidth(32)) ram_2 (
    .addr(store_addr_in), .we(store_enable), .clk(clock), .din(store_write_in));  // open: oe, dout
  Register #(.width(32)) InstFetch (.D(ram_1_dout), .clk(clock), .Q(InstFetch_q));  // open: en, clr
  Translator translator_1 (
    .opCode(InstFetch_q[6:0]), .funct3(InstFetch_q[14:12]), .funct7(InstFetch_q[31:25]),
    .TranslatedC(translator_1_translatedc));
  Clock clock_1 (.out(clock));
  Register #(.width(32)) store_offset (
    .D({{20{1'b0}}, InstFetch_q[31:25], InstFetch_q[11:7]}), .clk(clock), .Q(store_offset_q));  // open: en, clr
  Register #(.width(5)) OpCode (.D(translator_1_translatedc), .clk(clock), .Q(OpCode_q));  // open: en, clr
  Register #(.width(5)) u_Destino (.D(InstFetch_q[11:7]), .clk(clock), .Q(Destino_q));  // open: en, clr
  Register #(.width(5)) NOp1 (.D(InstFetch_q[19:15]), .clk(clock), .Q(NOp1_q));  // open: en, clr
  Register #(.width(5)) NOp2 (.D(InstFetch_q[24:20]), .clk(clock), .Q(NOp2_q));  // open: en, clr
  Register #(.width(32)) Imm (.D({{20{1'b0}}, InstFetch_q[31:20]}), .clk(clock), .Q(Imm_q));  // open: en, clr
  Registros Regs (
    .clk(clock), .writeDestiny(Destino), .writeEnable(Write), .nOp1(NOp1_q), .nOp2(NOp2_q),
    .writeData(WriteData), .op2(Regs_op2), .op1(Regs_op1));
  Register #(.width(32)) store_offset_2 (.D(store_offset_q), .clk(clock), .Q(store_offset_2_q));  // open: en, clr
  Register #(.width(5)) OpCode2 (.D(OpCode_q), .clk(clock), .Q(OpCode2_q));  // open: en, clr
  Register #(.width(5)) Destino2 (.D(Destino_q), .clk(clock), .Q(Destino2_q));  // open: en, clr
  Register #(.width(32)) Op1 (.D(Regs_op1), .clk(clock), .Q(store_base_position));  // open: en, clr
  Register #(.width(32)) Op2 (.D(Regs_op2), .clk(clock), .Q(store_write_data));  // open: en, clr
  Register #(.width(32)) Imm2 (.D(Imm_q), .clk(clock), .Q(Imm2_q));  // open: en, clr
  Adder #(.width(32)) adder_1 (.a(store_offset_2_q), .b(store_base_position), .out(adder_1_out));  // open: cin, cout
  ALU ALU1 (.opCode(OpCode2_q), .op1(store_base_position), .op2(store_write_data), .imm(Imm2_q), .result(ALU1_result));
  Multiplexer #(.select(5), .width(32)) multiplexer_1 (
    .in0(ALU1_result), .in1(ALU1_result), .in2(ALU1_result), .in3(ALU1_result), .in4(ALU1_result),
    .in5(ALU1_result), .in6(ALU1_result), .in7(ALU1_result), .in8(ALU1_result), .in9(ALU1_result),
    .in10(ALU1_result), .in11(ALU1_result), .in14(ALU1_result), .in15(ALU1_result), .out(multiplexer_1_out),
    .sel(OpCode2_q));  // open: in12, in13, in16, in17, in18, in19, in20, in21, in22, in23, in24, in25, in26, in27, in28, in29, in30, in31
  Register #(.width(32)) store_data (.D(store_write_data), .clk(clock), .Q(store_write_in));  // open: en, clr
  Register #(.width(14)) store_addr (.D(adder_1_out[13:0]), .clk(clock), .Q(store_addr_in));  // open: en, clr
  Register #(.width(5)) OpCode3 (.D(OpCode2_q), .clk(clock), .Q(OpCode3_q));  // open: en, clr
  Register #(.width(5)) Destino3 (.D(Destino2_q), .clk(clock), .Q(Destino));  // open: en, clr
  Register #(.width(32)) Resultado (.D(multiplexer_1_out), .clk(clock), .Q(WriteData));  // open: en, clr
  Decoder #(.select(5)) decoder_1 (
    .out0(decoder_1_out0), .out1(decoder_1_out1), .out2(decoder_1_out2), .out3(decoder_1_out3),
    .out4(decoder_1_out4), .out5(decoder_1_out5), .out6(decoder_1_out6), .out7(decoder_1_out7),
    .out8(decoder_1_out8), .out9(decoder_1_out9), .out10(decoder_1_out10), .out11(decoder_1_out11),
    .out12(decoder_1_out12), .out13(store_enable), .out14(decoder_1_out14), .sel(OpCode3_q));  // open: out15, out16, out17, out18, out19, out20, out21, out22, out23, out24, out25, out26, out27, out28, out29, out30, out31, en
  Comparator #(.mode("unsigned"), .width(5)) comparator_1 (
    .a(OpCode3_q), .b(5'b01101), .eq(comparator_1_eq));  // open: gt, lt
  not not_1 (Write, comparator_1_eq);
  // OR_Gate or_1 has open pins: in1=decoder_1_out14, in2=decoder_1_out12, in3=decoder_1_out11, in4=decoder_1_out10, in5=decoder_1_out9, in6=decoder_1_out8, in7=decoder_1_out7, in8=decoder_1_out6, in9=decoder_1_out5, in10=decoder_1_out4, in11=decoder_1_out3, in12=decoder_1_out2, in13=decoder_1_out1, in14=decoder_1_out0, out=open

  // Notes on the sheet:
  //   Esto se va a convertir en cache, es temporal
  //   Esto se va a convertir en cache, es temporal
  //   El data forwarding / Elegir immediato en vez de registro tiene que ser en esta area
  //   Dependiendo de la instruccion, algo diferente tiene que salir
  //   Registro al que se escribira
  //   Datos a escribir en registro
  //   Este decoder nos dice si una instruccion escribe en registro
  //   Decide si debe escribirse algo en registro
  //   Puede que haya leido mal, entonces dejo el decoder aqui
  //   Viendo las instrucciones, parece que solo el SW (13 / 0d) no escribe en un registro
endmodule

module Registros (
  input  [4:0] nOp1,
  input  [4:0] nOp2,
  input  [31:0] writeData,
  input  [4:0] writeDestiny,
  input  writeEnable,
  input  clk,
  output [31:0] op1,
  output [31:0] op2
);

  wire decoder_1_out1, decoder_1_out2, decoder_1_out3, decoder_1_out4, decoder_1_out5, decoder_1_out6,
       decoder_1_out7, decoder_1_out8, decoder_1_out9, decoder_1_out10, decoder_1_out11, decoder_1_out12,
       decoder_1_out13, decoder_1_out14, decoder_1_out15, decoder_1_out16, decoder_1_out17, decoder_1_out18,
       decoder_1_out19, decoder_1_out20, decoder_1_out21, decoder_1_out22, decoder_1_out24, decoder_1_out25,
       decoder_1_out26, decoder_1_out27, decoder_1_out28, decoder_1_out29, decoder_1_out30, decoder_1_out31,
       not_1_out;
  wire [4:0] multiplexer_1_out;
  wire [31:0] x0_q, x1_q, x2_q, x3_q, x4_q, x5_q, x6_q, x7_q, x8_q, x9_q, x10_q, x11_q, x12_q, x13_q, x14_q,
       x15_q, x16_q, x17_q, x18_q, x19_q, x20_q, x21_q, x22_q, x23_q, x24_q, x25_q, x26_q, x27_q, x28_q,
       x29_q, x30_q, x31_q;

  not not_1 (not_1_out, writeEnable);
  Decoder #(.select(5)) decoder_1 (
    .out1(decoder_1_out1), .out2(decoder_1_out2), .out3(decoder_1_out3), .out4(decoder_1_out4),
    .out5(decoder_1_out5), .out6(decoder_1_out6), .out7(decoder_1_out7), .out8(decoder_1_out8),
    .out9(decoder_1_out9), .out10(decoder_1_out10), .out11(decoder_1_out11), .out12(decoder_1_out12),
    .out13(decoder_1_out13), .out14(decoder_1_out14), .out15(decoder_1_out15), .out16(decoder_1_out16),
    .out17(decoder_1_out17), .out18(decoder_1_out18), .out19(decoder_1_out19), .out20(decoder_1_out20),
    .out21(decoder_1_out21), .out22(decoder_1_out22), .out23(decoder_1_out7), .out24(decoder_1_out24),
    .out25(decoder_1_out25), .out26(decoder_1_out26), .out27(decoder_1_out27), .out28(decoder_1_out28),
    .out29(decoder_1_out29), .out30(decoder_1_out30), .out31(decoder_1_out31), .sel(multiplexer_1_out));  // open: out0, en
  Multiplexer #(.width(5)) multiplexer_1 (
    .in0(writeDestiny), .in1({5{1'b0}}), .out(multiplexer_1_out), .sel(not_1_out));
  Register #(.width(32)) x0 (.D(writeData), .Q(x0_q));  // open: en, clk, clr
  Register #(.width(32)) x1 (.D(writeData), .en(decoder_1_out1), .clk(clk), .Q(x1_q));  // open: clr
  Register #(.width(32)) x2 (.D(writeData), .en(decoder_1_out2), .clk(clk), .Q(x2_q));  // open: clr
  Register #(.width(32)) x3 (.D(writeData), .en(decoder_1_out3), .clk(clk), .Q(x3_q));  // open: clr
  Register #(.width(32)) x4 (.D(writeData), .en(decoder_1_out4), .clk(clk), .Q(x4_q));  // open: clr
  Register #(.width(32)) x5 (.D(writeData), .en(decoder_1_out5), .clk(clk), .Q(x5_q));  // open: clr
  Register #(.width(32)) x6 (.D(writeData), .en(decoder_1_out6), .clk(clk), .Q(x6_q));  // open: clr
  Register #(.width(32)) x7 (.D(writeData), .en(decoder_1_out7), .clk(clk), .Q(x7_q));  // open: clr
  Register #(.width(32)) x8 (.D(writeData), .en(decoder_1_out8), .clk(clk), .Q(x8_q));  // open: clr
  Register #(.width(32)) x9 (.D(writeData), .en(decoder_1_out9), .clk(clk), .Q(x9_q));  // open: clr
  Register #(.width(32)) x10 (.D(writeData), .en(decoder_1_out10), .clk(clk), .Q(x10_q));  // open: clr
  Register #(.width(32)) x11 (.D(writeData), .en(decoder_1_out11), .clk(clk), .Q(x11_q));  // open: clr
  Register #(.width(32)) x12 (.D(writeData), .en(decoder_1_out12), .clk(clk), .Q(x12_q));  // open: clr
  Register #(.width(32)) x13 (.D(writeData), .en(decoder_1_out13), .clk(clk), .Q(x13_q));  // open: clr
  Register #(.width(32)) x14 (.D(writeData), .en(decoder_1_out14), .clk(clk), .Q(x14_q));  // open: clr
  Register #(.width(32)) x15 (.D(writeData), .en(decoder_1_out15), .clk(clk), .Q(x15_q));  // open: clr
  Multiplexer #(.select(5), .width(32)) multiplexer_2 (
    .in0(x0_q), .in1(x1_q), .in2(x2_q), .in3(x3_q), .in4(x4_q), .in5(x5_q), .in6(x6_q), .in7(x7_q),
    .in8(x8_q), .in9(x9_q), .in10(x10_q), .in11(x11_q), .in12(x12_q), .in13(x13_q), .in14(x14_q),
    .in15(x15_q), .in16(x16_q), .in17(x17_q), .in18(x18_q), .in19(x19_q), .in20(x20_q), .in21(x21_q),
    .in22(x22_q), .in23(x23_q), .in24(x24_q), .in25(x25_q), .in26(x26_q), .in27(x27_q), .in28(x28_q),
    .in29(x29_q), .in30(x30_q), .in31(x31_q), .out(op1), .sel(nOp1));
  Multiplexer #(.select(5), .width(32)) multiplexer_3 (
    .in0(x0_q), .in1(x1_q), .in2(x2_q), .in3(x3_q), .in4(x4_q), .in5(x5_q), .in6(x6_q), .in7(x7_q),
    .in8(x8_q), .in9(x9_q), .in10(x10_q), .in11(x11_q), .in12(x12_q), .in13(x13_q), .in14(x14_q),
    .in15(x15_q), .in16(x16_q), .in17(x17_q), .in18(x18_q), .in19(x19_q), .in20(x20_q), .in21(x21_q),
    .in22(x22_q), .in23(x23_q), .in24(x24_q), .in25(x25_q), .in26(x26_q), .in27(x27_q), .in28(x28_q),
    .in29(x29_q), .in30(x30_q), .in31(x31_q), .out(op2), .sel(nOp2));
  Register #(.width(32)) x16 (.D(writeData), .en(decoder_1_out16), .clk(clk), .Q(x16_q));  // open: clr
  Register #(.width(32)) x17 (.D(writeData), .en(decoder_1_out17), .clk(clk), .Q(x17_q));  // open: clr
  Register #(.width(32)) x18 (.D(writeData), .en(decoder_1_out18), .clk(clk), .Q(x18_q));  // open: clr
  Register #(.width(32)) x19 (.D(writeData), .en(decoder_1_out19), .clk(clk), .Q(x19_q));  // open: clr
  Register #(.width(32)) x20 (.D(writeData), .en(decoder_1_out20), .clk(clk), .Q(x20_q));  // open: clr
  Register #(.width(32)) x21 (.D(writeData), .en(decoder_1_out21), .clk(clk), .Q(x21_q));  // open: clr
  Register #(.width(32)) x22 (.D(writeData), .en(decoder_1_out22), .clk(clk), .Q(x22_q));  // open: clr
  Register #(.width(32)) x23 (.D(writeData), .en(decoder_1_out7), .clk(clk), .Q(x23_q));  // open: clr
  Register #(.width(32)) x24 (.D(writeData), .en(decoder_1_out24), .clk(clk), .Q(x24_q));  // open: clr
  Register #(.width(32)) x25 (.D(writeData), .en(decoder_1_out25), .clk(clk), .Q(x25_q));  // open: clr
  Register #(.width(32)) x26 (.D(writeData), .en(decoder_1_out26), .clk(clk), .Q(x26_q));  // open: clr
  Register #(.width(32)) x27 (.D(writeData), .en(decoder_1_out27), .clk(clk), .Q(x27_q));  // open: clr
  Register #(.width(32)) x28 (.D(writeData), .en(decoder_1_out28), .clk(clk), .Q(x28_q));  // open: clr
  Register #(.width(32)) x29 (.D(writeData), .en(decoder_1_out29), .clk(clk), .Q(x29_q));  // open: clr
  Register #(.width(32)) x30 (.D(writeData), .en(decoder_1_out30), .clk(clk), .Q(x30_q));  // open: clr
  Register #(.width(32)) x31 (.D(writeData), .en(decoder_1_out31), .clk(clk), .Q(x31_q));  // open: clr
endmodule

// VHDL entity not_gate, as the project stores it:
library IEEE;
use IEEE.STD_LOGIC_1164.ALL;

entity not_gate is
    Port ( 
        input  : in  STD_LOGIC;
        output : out STD_LOGIC
    );
end not_gate;

architecture behavioral of not_gate is
begin
    output <= not input;
end behavioral;

// VHDL entity ALU, as the project stores it:
LIBRARY ieee;
USE ieee.std_logic_1164.all;
USE ieee.numeric_std.all;

ENTITY ALU IS
  PORT (
    	opCode	: IN std_logic_vector(4 DOWNTO 0); -- codigo de operacion (5 bits)
	op1		: IN std_logic_vector(31 DOWNTO 0); -- operando 1 (32 bits)
	op2		: IN std_logic_vector(31 DOWNTO 0); -- operando 2 (32 bits)
    	imm		: IN std_logic_vector(31 DOWNTO 0); -- immediato (32 bits)
    	result   	: OUT std_logic_vector(31 DOWNTO 0)  -- resultado de la operacion (32 bits)
  );
END ALU;

--------------------------------------------------------------------------------
-- ALU Architecture Implementation
--------------------------------------------------------------------------------

ARCHITECTURE TypeArchitecture OF ALU IS
BEGIN
    PROCESS(opCode, op1, op2)
    BEGIN
        CASE opCode IS
            WHEN "00000" => -- ADD
                result <= std_logic_vector(signed(op1) + signed(op2));
            
            WHEN "00001" => -- SUB
                result <= std_logic_vector(signed(op1) - signed(op2));
            
            WHEN "00010" => -- ADDI
                result <= std_logic_vector(signed(op1) + signed(imm));
            
            WHEN "00011" => -- AND
                result <= op1 AND op2;
            
            WHEN "00100" => -- OR
                result <= op1 OR op2;
            
            WHEN "00101" => -- XOR
                result <= op1 XOR op2;
            
            WHEN "00110" => -- ANDI
                result <= op1 AND imm;
            
            WHEN "00111" => -- ORI
                result <= op1 OR imm;

            WHEN "01000" => -- XORI
                result <= op1 XOR imm;
            
            WHEN OTHERS =>
                result <= (OTHERS => '0');
        END CASE;
    END PROCESS;

END TypeArchitecture;

// VHDL entity Translator, as the project stores it:
LIBRARY ieee;
USE ieee.std_logic_1164.all;

ENTITY Translator IS
  PORT (
  ------------------------------------------------------------------------------
  --Insert input ports below
    opCode    	: IN  std_logic_vector(6 DOWNTO 0); -- Op Code que describe el tipo de instruccion
    funct3     	: IN  std_logic_vector(2 DOWNTO 0); -- funct3 que describe la instruccion especifica
    funct7     	: IN  std_logic_vector(6 DOWNTO 0); -- funct7 que describe la instruccion especifica (solo en R-Type)
  ------------------------------------------------------------------------------
  --Insert output ports below
    TranslatedC	: OUT std_logic_vector(4 DOWNTO 0)  -- Codigo traducido
    );
END Translator;

--------------------------------------------------------------------------------
--Complete your VHDL description below
--------------------------------------------------------------------------------

ARCHITECTURE TypeArchitecture OF Translator IS

BEGIN
    PROCESS(opCode, funct3, funct7)
    BEGIN
        CASE opCode IS
            WHEN "0110011" => -- R-Type
                IF funct3 = "000" and funct7 = "0000000" THEN
                	TranslatedC <= "00000"; 
                END IF;
            WHEN "0100011" => -- S-Type
            	IF funct3 = "010"  THEN -- sw
                	TranslatedC <= "01101"; 
                END IF;
            WHEN OTHERS =>
            	TranslatedC <= "11111";
        END CASE;
    END PROCESS;

END TypeArchitecture;
